# Fritzing sketch brewery-water-controller (saved by Fritzing 0.9.4)
circuit board: 8.46667cm x 5.64444cm
breadboards: 1

parts:
  Button_R = Resistor [tolerance=±5% resistance=10k package="0805 [SMD]"]
  Q1 = MOSFET-NCHANNEL [package=to220v]
  Flow_R = Resistor [tolerance=±5% resistance=10k package="0805 [SMD]"]
  LCD_I2C_Connector = Header 4 [package=screwterminal-3.5mm-4_lock]
  Flow_Meter_Connector = JST-03JQ-BT [part_number=JST-JQ-BT package=THT]
  Solenoid_R = Resistor [tolerance=±5% resistance=10k package="0402 [SMD]"]
  D1 = Rectifier Diode [part_number=1N4001 package="300 mil [THT]"]
  Solenoid_Connector = JST-03JQ-BT [part_number=JST-JQ-BT package=THT]
  S1 = Pushbutton [package="[THT]"]
  Part1 = Arduino Uno (Rev3)

nets (from the breadboard view):
  N1: Button_R.Pin_0, Q1.S, LCD_I2C_Connector.1, Flow_Meter_Connector.pin2, Solenoid_R.Pin_1, Part1.GND
  N2: Button_R.Pin_1, S1.Pin_3, S1.Pin_4, Part1.D3_PWM
  N3: Q1.G, Solenoid_R.Pin_0, Part1.D4
  N4: Q1.D, D1.anode, Solenoid_Connector.pin3
  N5: Flow_R.Pin_0, Flow_Meter_Connector.pin3, Part1.D2
  N6: Flow_R.Pin_1, LCD_I2C_Connector.2, Flow_Meter_Connector.pin1, S1.Pin_1, S1.Pin_2, Part1.5V
  N7: LCD_I2C_Connector.3, Part1.A4/SDA
  N8: LCD_I2C_Connector.4, Part1.A5/SCL
  N9: D1.cathode, Solenoid_Connector.pin2, Solenoid_Connector.pin1, Part1.VIN
